# Fritzing sketch 30.007 SYSTEMS DIAG (saved by Fritzing 0.9.3b)

parts:
  U1 = Mini-360 DC-DC Buck converter [package=THT]
  JACK1 = 2.1mm Barrel Jack with Terminal Block
  U2 = prefix0000
  Raspberry_Pi_1 = Raspberry Pi 3 [part_number=RPI-3-V1.2]
  Mod1 = KY-019 5V Relay Module [package="Breakout board"]
  M2 = Stepper Motor - Bipolar  # not connected
  U4 = Mini-360 DC-DC Buck converter [package=THT]
  M1 = Stepper Motor - Bipolar
  M3 = DC Motor
  DS1 = DS18B20 1-Wire Temperature Sensor Probe Cable  # not connected
  U5 = TCM8240MD [package=tcm8240md]  # not connected
  J1 = Peltier Element
  Mod2 = KY-019 5V Relay Module [package="Breakout board"]

nets:
  N1: U1.IN-, JACK1.NEG, U2.connector5, Mod1.-, U4.IN-, Mod2.-, Mod2.NO
  N2: U1.IN+, JACK1.POS, U2.connector4, U4.IN+, J1.pin2
  N3: U1.OUT+, M3.pin_2
  N4: U1.OUT-, Mod1.NO
  N5: U2.connector0, M1.D
  N6: U2.connector1, M1.C
  N7: U2.connector2, M1.B
  N8: U2.connector3, M1.A
  N9: U2.connector6, U2.connector8, U2.connector10, Raspberry_Pi_1.GND
  N10: U2.connector7, Raspberry_Pi_1.GPIO16
  N11: U2.connector9, Raspberry_Pi_1.GPIO20
  N12: U2.connector11, Raspberry_Pi_1.GPIO21
  N13: Raspberry_Pi_1.GPIO4, Mod2.S
  N14: Raspberry_Pi_1.GPIO14, Mod1.S
  N15: Raspberry_Pi_1.5V, Mod1.+, Mod2.+
  N16: Mod1.Common, M3.pin_1
  N17: J1.pin1, Mod2.Common

notes:
  stepdown 12v to 7v
  12v 6a input mains
  stepdown 12v to 5v
  (should use this for all 5v applications like relays but can test with 5v from rpi first)
  Pipette
  Centrifuge
  TEC2 12v

custom parts:
  Mini-360 DC-DC Buck converter: Mini-360 DC-DC Buck converter. Tiny buck step down voltage converter, input voltage 4.75 to 23V output 1 to 17V adjustable. Available from ebay and the like.
  KY-019 5V Relay Module: KY-019 5V Relay module, used to control AC circuits. (Special thanks to vanepp for fixing the PCB holes and other errors)
